// Logisim project calculator.circ as structural Verilog: 1 circuit, main circuit main
module main (
  input  in_1,
  input  in_2,
  input  in_3,
  input  in_4,
  input  in_5,
  input  in_6,
  input  in_7,
  input  in_8,
  input  in_9,
  input  in_10,
  input  in_11,
  input  in_12,
  input  in_13,
  input  in_14,
  input  in_15,
  input  in_16,
  input  in_17,
  input  in_18,
  input  in_19,
  input  in_20,
  input  in_21,
  input  in_22,
  input  in_23,
  input  in_24,
  input  in_25,
  input  in_26,
  input  in_27,
  input  in_28,
  input  in_29,
  input  in_30,
  input  in_31,
  input  in_32,
  input  in_33,
  input  in_34,
  input  in_35,
  input  in_36,
  input  in_37,
  input  in_38,
  input  in_39,
  input  in_40,
  input  in_41,
  input  in_42,
  input  in_43,
  input  in_44,
  input  in_45,
  input  in_46,
  input  in_47,
  input  in_48,
  input  in_49,
  input  in_50,
  input  in_51,
  input  in_52,
  input  in_53,
  input  in_54,
  input  in_55,
  input  in_56,
  input  in_57,
  input  in_58,
  input  in_59,
  input  in_60,
  input  in_61,
  input  in_62,
  input  in_63,
  input  in_64,
  input  in_65,
  input  in_66,
  input  in_67,
  input  in_68,
  input  in_69,
  input  in_70,
  input  in_71,
  input  in_72,
  input  in_73,
  input  in_74,
  input  in_75,
  input  in_76,
  input  in_77,
  input  in_78,
  input  in_79,
  input  in_80,
  input  in_81,
  input  in_82,
  input  in_83,
  input  in_84,
  input  in_85,
  input  in_86,
  input  in_87,
  input  in_88,
  input  in_89,
  input  in_90,
  input  in_91,
  input  in_92,
  input  in_93,
  input  in_94,
  input  in_95,
  input  in_96
);

  wire main_1_out_13, main_2_equality_check, main_3_p1, main_3_p2, main_3_p3, main_3_p4, main_3_p5,
       main_3_p6, main_3_p7, main_3_p8, main_3_p9, main_3_p10, main_3_p11, main_3_p12, main_4_out_13,
       main_5_out_13, main_5_out_14, main_5_out_15, main_5_out_16, main_5_out_17, main_5_out_18,
       main_5_out_19, main_6_out_13, main_6_out_14, main_6_out_16, main_6_out_17, main_6_out_18,
       main_6_output, main_7_p1, main_7_p2, main_7_p3, main_7_p4, main_7_p5, main_7_p6, main_8_out_13,
       main_8_out_14, main_8_out_15, main_8_out_16, main_8_out_17, main_8_out_18, undriven, undriven_2,
       undriven_3, undriven_4, undriven_5, undriven_6;

  LED led_1 (.in(main_1_out_13));
  LED led_2 (.in(main_2_equality_check));
  a_greater_than_b_main main_1 (
    .in_1(in_1), .in_2(in_2), .in_3(in_3), .in_4(in_4), .in_5(in_5), .in_6(in_6), .in_7(in_19), .in_8(in_20),
    .in_9(in_21), .in_10(in_22), .in_11(in_23), .in_12(in_24), .out_13(main_1_out_13));
  LED led_3 (.in(main_3_p5));
  LED led_4 (.in(main_3_p1));
  LED led_5 (.in(main_3_p7));
  LED led_6 (.in(main_3_p3));
  LED led_7 (.in(main_3_p6));
  LED led_8 (.in(main_3_p4));
  LED led_9 (.in(main_3_p2));
  LED led_10 (.in(main_3_p8));
  equality_check_main main_2 (
    .Equality_Check(main_2_equality_check), .in_1(in_67), .in_2(in_68), .Number_A(in_69), .in_4(in_70),
    .in_5(in_71), .in_6(in_72), .in_7(in_79), .in_8(in_80), .in_9(in_81), .in_10(in_82), .in_11(in_83),
    .in_12(in_84));
  LED led_11 (.in(main_3_p11));
  LED led_12 (.in(main_3_p9));
  // division_main main_3: pin names not known; wires that end beside it: main_3_p1, main_3_p2, main_3_p3, main_3_p4, main_3_p5, main_3_p6, main_3_p7, main_3_p8, main_3_p9, main_3_p10, main_3_p11, main_3_p12, in_37, in_49
  LED led_13 (.in(main_3_p10));
  LED led_14 (.in(main_3_p12));
  LED led_15 (.in(main_5_out_15));
  LED led_16 (.in(main_5_out_13));
  LED led_17 (.in(main_5_out_14));
  LED led_18 (.in(main_4_out_13));
  LED led_19 (.in(main_5_out_19));
  LED led_20 (.in(main_5_out_17));
  LED led_21 (.in(main_5_out_16));
  LED led_22 (.in(main_5_out_18));
  a_less_than_b_main main_4 (
    .in_7(in_85), .in_8(in_86), .in_9(in_87), .in_10(in_88), .in_11(in_89), .in_12(in_90), .in_1(in_73),
    .in_2(in_74), .in_3(in_75), .in_4(in_76), .in_5(in_77), .in_6(in_78), .out_13(main_4_out_13));
  addition_main main_5 (
    .in_1(in_7), .in_2(in_8), .in_3(in_9), .in_4(in_10), .in_5(in_11), .in_6(in_12), .in_7(in_25),
    .in_8(in_26), .in_9(in_27), .in_10(in_28), .in_11(in_29), .in_12(in_30), .out_13(main_5_out_13),
    .out_14(main_5_out_14), .out_15(main_5_out_15), .out_16(main_5_out_16), .out_17(main_5_out_17),
    .out_18(main_5_out_18), .out_19(main_5_out_19));
  LED led_23 (.in(main_6_out_13));
  LED led_24 (.in(undriven_4));
  LED led_25 (.in(undriven_3));
  LED led_26 (.in(undriven_2));
  LED led_27 (.in(undriven));
  LED led_28 (.in(main_6_out_16));
  LED led_29 (.in(main_6_out_17));
  LED led_30 (.in(main_6_output));
  LED led_31 (.in(main_6_out_14));
  LED led_32 (.in(undriven_5));
  LED led_33 (.in(main_7_p1));
  LED led_34 (.in(main_7_p2));
  LED led_35 (.in(undriven_6));
  LED led_36 (.in(main_6_out_18));
  memory_main main_6 (
    .Address(in_91), .in_2(in_92), .Write(in_93), .in_4(in_94), .Read(in_95), .Initialise(in_96),
    .in_7(in_61), .in_8(in_62), .Input(in_63), .in_10(in_64), .in_11(in_65), .in_12(in_66),
    .out_13(main_6_out_13), .out_14(main_6_out_14), .Output(main_6_output), .out_16(main_6_out_16),
    .out_17(main_6_out_17), .out_18(main_6_out_18));
  LED led_37 (.in(main_8_out_17));
  LED led_38 (.in(main_8_out_15));
  LED led_39 (.in(main_8_out_18));
  LED led_40 (.in(main_8_out_16));
  LED led_41 (.in(main_7_p5));
  LED led_42 (.in(main_7_p4));
  LED led_43 (.in(main_7_p3));
  LED led_44 (.in(main_7_p6));
  // multiplication_main main_7: pin names not known; wires that end beside it: main_7_p1, main_7_p2, main_7_p3, main_7_p4, main_7_p5, main_7_p6
  LED led_45 (.in(main_8_out_14));
  LED led_46 (.in(main_8_out_13));
  subtraction_main main_8 (
    .in_7(in_31), .in_8(in_32), .in_9(in_33), .in_10(in_34), .in_11(in_35), .in_12(in_36),
    .out_15(main_8_out_15), .out_16(main_8_out_16), .out_17(main_8_out_17), .out_18(main_8_out_18),
    .in_1(in_13), .in_2(in_14), .in_3(in_15), .in_4(in_16), .in_5(in_17), .in_6(in_18),
    .out_13(main_8_out_13), .out_14(main_8_out_14));
endmodule
